// Logisim project Warner8016.circ as structural Verilog: 11 circuits, main circuit 8016
module _8016 (
  input  [7:0] Control_In,
  output ROM_LOAD,
  output [7:0] EAX,
  output RAM_READ,
  output [7:0] ECX,
  output [7:0] Address,
  output [7:0] ALU_Data,
  output RAM_LOAD,
  output [7:0] EDX,
  output [7:0] EBX,
  output [7:0] ESI,
  output [7:0] EDI,
  output [7:0] DATA_OUT,
  output [7:0] ESP,
  output [7:0] Address_2,
  output [7:0] EBP,
  output [7:0] DATA_OUT_2,
  output [7:0] DATA_IN,
  output [3:0] out_19,
  output [7:0] Reg_Data,
  output [7:0] Reg_Out,
  output OF,
  output [7:0] out_23,
  output [3:0] out_24,
  output [7:0] out_25,
  output [7:0] Data_1,
  output [7:0] Address_3,
  output [7:0] out_28,
  output [7:0] Data_2,
  output [7:0] out_30,
  output [6:0] out_31,
  output [3:0] out_32,
  output [3:0] out_33,
  output _5,
  output out_35,
  output out_36,
  output out_37
);

  wire _2_3_Reg, ALU_A_READ, ALU_B_READ, ALU_B_READ_0, clock_1_out, clock_2_out, Instruction_Read,
       Mr_rM_1_Reg, Mr_rM_1_Reg_2_3_Reg, MUL, multiplexer_2_out, multiplexer_5_out, not_1_out, or_1_out,
       pc_1_out_5, pc_1_out_6, pc_1_out_7, pc_1_out_8, Read_ID_A, Read_ID_B, Reg_Clear, Reg_Route, Reg_Write,
       Route_B;
  wire [3:0] _1R, _2R, _3R, Mr_rM_Address;
  wire [7:0] A_q, alu_1_mout, B_q, controlled_buffer_1_out, Instruction,
       instruction_fetch_1_instruction_address, multiplexer_3_out;
  wire [15:0] PC_OUT;

  Multiplexer #(.enable("false")) multiplexer_1 (.in0(1'b0), .in1(Route_B), .sel(Route_B));  // open: out
  Multiplexer #(.enable("false")) multiplexer_2 (.in0(1'b0), .in1(1'b0), .out(multiplexer_2_out), .sel(1'b0));
  Multiplexer #(.width(8), .enable("false")) multiplexer_3 (
    .in0(ALU_Data), .in1({8{1'b0}}), .out(multiplexer_3_out), .sel(ALU_B_READ_0));
  Clock clock_1 (.out(clock_1_out));
  Registers registers_1 (
    .IN(out_30), .Write(Reg_Write), .Select(out_19), .CLR(Reg_Clear), .out_14(out_33), .OUT(out_28),
    .EAX(EAX), .ECX(ECX), .EDX(EDX), .EBX(EBX), .ESI(ESI), .EDI(EDI), .ESP(ESP), .EBP(EBP));
  Register B (.D(multiplexer_3_out), .en(ALU_B_READ), .Q(B_q), .clk(clock_1_out), .clr(1'b0));
  Register A (.D(ALU_Data), .en(ALU_A_READ), .Q(A_q), .clk(clock_1_out), .clr(1'b0));
  ALU alu_1 (.Route(Route_B), .SUB(multiplexer_2_out), .OF(OF), .B(B_q), .A(A_q), .OUT(out_25), .mOut(alu_1_mout));
  Multiplexer #(.width(8), .enable("false")) multiplexer_4 (.in0(out_25), .in1(alu_1_mout), .out(out_23), .sel(MUL));
  or or_1 (or_1_out, RAM_READ, RAM_LOAD);
  Data_Router data_router_1 (
    .ALU_Data(ALU_Data), .Instruction_Read(Instruction_Read), .MR_RM_Reg_Address(Mr_rM_Address),
    ._1st_Reg(_1R), ._2nd_Reg(_2R), ._3rd_Reg(_3R), .External_Data_Out(DATA_OUT), .External_Data_In(DATA_IN),
    .Register_Out(out_30), .Register_In(out_28), .Reg_Select(out_19), .Instruction(Instruction),
    .Mr_rM_1_Reg(Mr_rM_1_Reg), .ALU_In(out_23), ._2_3_Reg(_2_3_Reg),
    .Mr_rM_1_Reg_2_3_Reg(Mr_rM_1_Reg_2_3_Reg), .Data_Select(Reg_Route));  // open: External_Data_In_2, Control_In
  RAM #(.bus("separate")) ram_1 (
    .addr(Address), .din(DATA_IN), .data(DATA_IN), .str(RAM_READ), .sel(or_1_out), .ld(RAM_LOAD));  // open: clk, clr
  Instruction_Decoder instruction_decoder_1 (
    .IN(Instruction), ._1_Write(Read_ID_A), ._2_Write(Read_ID_B), .MR_RM_Reg_Address(Mr_rM_Address),
    ._1st_Reg(_1R), ._2nd_Reg(_2R), ._3rd_Reg(_3R), .Data_1(Data_1), .Data_2(Data_2), .Instruction(out_31),
    .Address_Bus(Address), .Data_Bus(DATA_OUT));  // open: CLEAR
  LED led_1 (.in(ALU_A_READ));
  LED led_2 (.in(ALU_B_READ));
  LED led_3 (.in(Read_ID_A));
  LED led_4 (.in(Read_ID_B));
  LED led_5 (.in(ALU_B_READ_0));
  LED led_6 (.in(ALU_B_READ_0));
  CONTROL control_1 (
    .COUNTER_IN(PC_OUT), .Instruction(out_31), .RAM_LOAD(RAM_LOAD), .RAM_STORE(RAM_READ),
    .ALU_A_READ(ALU_A_READ), .ALU_B_READ(ALU_B_READ), .ALU_B_0(ALU_B_READ_0), .Reg_Write(Reg_Write),
    .nMr_rM_1_Reg(Mr_rM_1_Reg), .nMr_rM_1_Reg_2_3_Reg(Mr_rM_1_Reg_2_3_Reg), .n2_3_Reg(_2_3_Reg),
    .nReg_Route(Reg_Route), .Multiply(MUL), .Rotue_B(Route_B));  // open: out_15, out_16, out_17, out_18
  LED led_7 (.in(Reg_Clear));
  LED led_8 (.in(Reg_Write));
  PC pc_1 (
    .out_5(pc_1_out_5), .out_6(pc_1_out_6), .out_7(pc_1_out_7), .out_8(pc_1_out_8), .COUNTER_OUT(PC_OUT));  // open: Count_Enable, Counter_Value, out_4, out_10, out_11, out_12, out_13, out_14, out_15, out_16, out_17, out_18, out_19, out_20, Reset
  Instruction_Fetch instruction_fetch_1 (
    .Fetch_First(pc_1_out_5), .Fetch_Second(pc_1_out_6), .StepUp_1(pc_1_out_7), .StepUp2(pc_1_out_8),
    .ROM_LOAD(ROM_LOAD), .ID_A_READ(Read_ID_A), .ID_B_READ(Read_ID_B), .Instruction_Read(Instruction_Read),
    .Instruction_Address(instruction_fetch_1_instruction_address));  // open: ALU_A_READ, ALU_B_READ_READ_0
  assign controlled_buffer_1_out = RAM_LOAD ? Address : 8'bz;  // Controlled_Buffer controlled_buffer_1
  Clock clock_2 (.out(clock_2_out));
  not not_1 (not_1_out, RAM_LOAD);
  Multiplexer #(.enable("false")) multiplexer_5 (.in0(1'b0), .in1(RAM_READ), .out(multiplexer_5_out), .sel(RAM_READ));
  ROM rom_1 (.addr(instruction_fetch_1_instruction_address), .data(DATA_IN), .sel(ROM_LOAD));
  RAM ram_2 (
    .addr(controlled_buffer_1_out), .sel(multiplexer_5_out), .clk(clock_2_out), .ld(not_1_out));  // open: data, clr

  assign Address_3 = Address;
  assign DATA_OUT_2 = DATA_OUT;
  assign out_32 = out_19;
  assign Reg_Data = out_30;
  assign Reg_Out = out_28;

  // Other names for the same wires on the sheet: RAM_STORE = RAM_READ; Reg_S[3:0] = out_19

  // Notes on the sheet:
  //   TEMPORARY, REPLCE LATER
  //   ONCE IMPLEMENTED FULLY
  //   NOT USED, SEE OTHER RAM BLOCK
  //   contents of rom_1 (hex, n*v repeats v):
  //   20 0 20 11 20 22 20 33 50 14 52 35 44 50 30 4
endmodule

module ALU (
  input  [7:0] B,
  input  [7:0] A,
  input  Route,
  input  SUB,
  output [7:0] mOut,
  output OF,
  output [7:0] OUT
);

  wire [7:0] multiplexer_1_out, multiplexer_2_out, not_1_out;

  Multiplexer #(.width(8), .enable("false")) multiplexer_1 (
    .in0({8{1'b0}}), .in1(B), .out(multiplexer_1_out), .sel(Route));
  assign not_1_out = ~multiplexer_1_out;  // NOT_Gate not_1, 8 bits wide
  Multiplexer #(.width(8), .enable("false")) multiplexer_2 (
    .in0(multiplexer_1_out), .in1(not_1_out), .out(multiplexer_2_out), .sel(SUB));
  _8_Bit_Adder u_8_bit_adder_1 (.Bi(multiplexer_2_out), .Ai(A), .Ci(SUB), .Co(OF), .OUT(OUT));
  Multiplier multiplier_1 (.a(A), .b(multiplexer_1_out), .out(mOut));  // open: cin, cout
endmodule

// ADD
module _8_Bit_Adder (
  input  [7:0] Bi,
  input  [7:0] Ai,
  input  Ci,
  output Co,
  output [7:0] OUT
);

  wire and_1_out, and_2_out, and_3_out, and_4_out, and_5_out, and_6_out, and_7_out, and_8_out, and_9_out,
       and_10_out, and_11_out, and_12_out, and_13_out, and_14_out, and_15_out, and_16_out, or_2_out,
       or_3_out, or_4_out, or_5_out, or_6_out, or_7_out, or_8_out, xor_1_out, xor_3_out, xor_5_out,
       xor_7_out, xor_9_out, xor_11_out, xor_14_out, xor_15_out;

  and and_1 (and_1_out, Bi[7], Ai[7]);
  and and_2 (and_2_out, or_2_out, xor_1_out);
  or or_1 (Co, and_1_out, and_2_out);
  xor xor_1 (xor_1_out, Bi[7], Ai[7]);
  and and_3 (and_3_out, Bi[6], Ai[6]);
  xor xor_2 (OUT[7], or_2_out, xor_1_out);
  xor xor_3 (xor_3_out, Bi[6], Ai[6]);
  and and_4 (and_4_out, or_3_out, xor_3_out);
  xor xor_4 (OUT[6], or_3_out, xor_3_out);
  or or_2 (or_2_out, and_3_out, and_4_out);
  and and_5 (and_5_out, Bi[5], Ai[5]);
  or or_3 (or_3_out, and_5_out, and_6_out);
  xor xor_5 (xor_5_out, Bi[5], Ai[5]);
  xor xor_6 (OUT[5], or_4_out, xor_5_out);
  and and_6 (and_6_out, or_4_out, xor_5_out);
  and and_7 (and_7_out, or_5_out, xor_7_out);
  and and_8 (and_8_out, Bi[4], Ai[4]);
  or or_4 (or_4_out, and_8_out, and_7_out);
  xor xor_7 (xor_7_out, Bi[4], Ai[4]);
  xor xor_8 (OUT[4], or_5_out, xor_7_out);
  and and_9 (and_9_out, or_6_out, xor_9_out);
  and and_10 (and_10_out, Bi[3], Ai[3]);
  or or_5 (or_5_out, and_10_out, and_9_out);
  xor xor_9 (xor_9_out, Bi[3], Ai[3]);
  xor xor_10 (OUT[3], or_6_out, xor_9_out);
  and and_11 (and_11_out, Bi[2], Ai[2]);
  and and_12 (and_12_out, or_7_out, xor_11_out);
  or or_6 (or_6_out, and_11_out, and_12_out);
  xor xor_11 (xor_11_out, Bi[2], Ai[2]);
  and and_13 (and_13_out, Bi[1], Ai[1]);
  xor xor_12 (OUT[2], or_7_out, xor_11_out);
  xor xor_13 (OUT[1], or_8_out, xor_14_out);
  and and_14 (and_14_out, or_8_out, xor_14_out);
  or or_7 (or_7_out, and_13_out, and_14_out);
  xor xor_14 (xor_14_out, Bi[1], Ai[1]);
  and and_15 (and_15_out, Bi[0], Ai[0]);
  xor xor_15 (xor_15_out, Bi[0], Ai[0]);
  xor xor_16 (OUT[0], Ci, xor_15_out);
  and and_16 (and_16_out, Ci, xor_15_out);
  or or_8 (or_8_out, and_15_out, and_16_out);
endmodule

// FA
module Full_adder (
  input  Ci,
  input  B,
  input  A,
  output Co,
  output OUT
);

  wire and_1_out, and_2_out, xor_1_out;

  and and_1 (and_1_out, B, A);
  or or_1 (Co, and_1_out, and_2_out);
  xor xor_1 (xor_1_out, B, A);
  xor xor_2 (OUT, Ci, xor_1_out);
  and and_2 (and_2_out, Ci, xor_1_out);
endmodule

// REG
module Registers (
  input  CLR,
  input  [7:0] IN,
  input  Write,
  input  [3:0] Select,
  output [7:0] OUT,
  output [7:0] EAX,
  output [7:0] ECX,
  output [7:0] EDX,
  output [7:0] EBX,
  output [7:0] ESI,
  output [7:0] EDI,
  output [7:0] ESP,
  output [7:0] EBP,
  output [3:0] out_14
);

  wire clock_1_out, EAX_out, EBP_out, EBX_out, ECX_out, EDI_out, EDX_out, ESI_out, ESP_out;
  wire [7:0] demultiplexer_1_out0, demultiplexer_1_out1, demultiplexer_1_out2, demultiplexer_1_out3,
       demultiplexer_1_out4, demultiplexer_1_out5, demultiplexer_1_out6, demultiplexer_1_out7;

  and u_EAX (EAX_out, Write, ~Select[0], ~Select[1], ~Select[2], ~Select[3]);  // AND_Gate
  and u_ECX (ECX_out, Write, Select[0], ~Select[1], ~Select[2], ~Select[3]);  // AND_Gate
  and u_EDX (EDX_out, Write, ~Select[0], Select[1], ~Select[2], ~Select[3]);  // AND_Gate
  and u_EBX (EBX_out, Write, Select[0], Select[1], ~Select[2], ~Select[3]);  // AND_Gate
  and u_ESI (ESI_out, Write, ~Select[0], ~Select[1], Select[2], ~Select[3]);  // AND_Gate
  and u_EDI (EDI_out, Write, Select[0], ~Select[1], Select[2], ~Select[3]);  // AND_Gate
  and u_ESP (ESP_out, Write, ~Select[0], Select[1], Select[2], ~Select[3]);  // AND_Gate
  and u_EBP (EBP_out, Write, Select[0], Select[1], Select[2], ~Select[3]);  // AND_Gate
  Demultiplexer #(.select(4), .width(8)) demultiplexer_1 (
    .out0(demultiplexer_1_out0), .out1(demultiplexer_1_out1), .out2(demultiplexer_1_out2),
    .out3(demultiplexer_1_out3), .out4(demultiplexer_1_out4), .out5(demultiplexer_1_out5),
    .out6(demultiplexer_1_out6), .out7(demultiplexer_1_out7), .in(IN), .sel(Select), .en(Write));  // open: out8, out9, out10, out11, out12, out13, out14, out15
  Clock clock_1 (.out(clock_1_out));
  Register EAX_2 (.D(demultiplexer_1_out0), .en(EAX_out), .Q(EAX), .clk(clock_1_out), .clr(CLR));
  Register ECX_2 (.D(demultiplexer_1_out1), .en(ECX_out), .Q(ECX), .clk(clock_1_out), .clr(CLR));
  Register EDX_2 (.D(demultiplexer_1_out2), .en(EDX_out), .Q(EDX), .clk(clock_1_out), .clr(CLR));
  Register EBX_2 (.D(demultiplexer_1_out3), .en(EBX_out), .Q(EBX), .clk(clock_1_out), .clr(CLR));
  Register ESI_2 (.D(demultiplexer_1_out4), .en(ESI_out), .Q(ESI), .clk(clock_1_out), .clr(CLR));
  Register EDI_2 (.D(demultiplexer_1_out5), .en(EDI_out), .Q(EDI), .clk(clock_1_out), .clr(CLR));
  Register ESP_2 (.D(demultiplexer_1_out6), .en(ESP_out), .Q(ESP), .clk(clock_1_out), .clr(CLR));
  Register EBP_2 (.D(demultiplexer_1_out7), .en(EBP_out), .Q(EBP), .clk(clock_1_out), .clr(CLR));
  Multiplexer #(.select(4), .width(8)) multiplexer_1 (
    .in0(EAX), .in1(ECX), .in2(EDX), .in3(EBX), .in4(ESI), .in5(EDI), .in6(ESP), .in7(EBP), .out(OUT),
    .sel(Select));  // open: in8, in9, in10, in11, in12, in13, in14, in15, en

  assign out_14 = Select;
endmodule

// ID
module Instruction_Decoder (
  input  CLEAR,
  input  [7:0] IN,
  input  _1_Write,
  input  _2_Write,
  output [6:0] Instruction,
  output [7:0] Data_1,
  output [7:0] Address_Bus,
  output [7:0] Data_2,
  output [7:0] Data_Bus,
  output [3:0] MR_RM_Reg_Address,
  output [3:0] _1st_Reg,
  output [3:0] _2nd_Reg,
  output [3:0] _3rd_Reg
);

  wire clock_1_out, irmovl_2_out, mrmovl_2_out, or_1_out, rmmovl_2_out;
  wire [7:0] demultiplexer_1_out0, demultiplexer_1_out1, demultiplexer_2_out0, demultiplexer_2_out1,
       multiplexer_1_out, multiplexer_2_out, multiplexer_4_out, undriven;

  Demultiplexer #(.width(8), .enable("false")) demultiplexer_1 (
    .out0(demultiplexer_1_out0), .out1(demultiplexer_1_out1), .in(IN), .sel(_2_Write));
  Clock clock_1 (.out(clock_1_out));
  Register b0__b7 (
    .D(demultiplexer_1_out0), .en(_1_Write), .Q({Data_1[7:4], _1st_Reg}), .clk(clock_1_out), .clr(CLEAR));
  Register b8__b15 (.D(demultiplexer_1_out1), .en(_2_Write), .Q({_2nd_Reg, _3rd_Reg}), .clk(clock_1_out), .clr(CLEAR));
  and nop (Instruction[0], ~Data_1[6], ~Data_1[5], ~Data_1[4]);  // AND_Gate
  and halt (Instruction[1], ~Data_1[6], ~Data_1[5], Data_1[4]);  // AND_Gate
  and mrmovl (Instruction[2], ~Data_1[6], Data_1[5], ~Data_1[4]);  // AND_Gate
  and rmmovl (Instruction[3], ~Data_1[6], Data_1[5], Data_1[4]);  // AND_Gate
  and addl (Instruction[5], Data_1[6], ~Data_1[5], ~Data_1[4]);  // AND_Gate
  and mull (Instruction[6], Data_1[6], ~Data_1[5], Data_1[4]);  // AND_Gate
  and irmovl (Instruction[4], Data_1[6], Data_1[5], ~Data_1[4]);  // AND_Gate
  and mrmovl_2 (mrmovl_2_out, ~Instruction[0], ~Instruction[1], Instruction[2], ~Instruction[3], ~Instruction[5], ~Instruction[6], ~Instruction[4]);  // AND_Gate
  and rmmovl_2 (rmmovl_2_out, ~Instruction[0], ~Instruction[1], ~Instruction[2], Instruction[3], ~Instruction[5], ~Instruction[6], ~Instruction[4]);  // AND_Gate
  and irmovl_2 (irmovl_2_out, ~Instruction[0], ~Instruction[1], ~Instruction[2], ~Instruction[3], ~Instruction[5], ~Instruction[6], Instruction[4]);  // AND_Gate
  or or_1 (or_1_out, rmmovl_2_out, irmovl_2_out, mrmovl_2_out);
  Multiplexer #(.width(8)) multiplexer_1 (
    .in0({_3rd_Reg, _1st_Reg}), .in1({_2nd_Reg, _3rd_Reg}), .out(multiplexer_1_out), .sel(mrmovl_2_out),
    .en(or_1_out));
  LED led_1 (.in(Instruction[0]));
  LED led_2 (.in(Instruction[1]));
  LED led_3 (.in(Instruction[2]));
  LED led_4 (.in(Instruction[3]));
  LED led_5 (.in(Instruction[5]));
  LED led_6 (.in(Instruction[6]));
  LED led_7 (.in(Instruction[4]));
  Multiplexer #(.width(8), .enable("false")) multiplexer_2 (
    .in0(undriven), .in1(multiplexer_1_out), .out(multiplexer_2_out), .sel(or_1_out));
  // NOT_Gate not_1 has open pins: in=or_1_out, out=open
  Demultiplexer #(.width(8), .enable("false")) demultiplexer_2 (
    .out0(demultiplexer_2_out0), .out1(demultiplexer_2_out1), .in(multiplexer_2_out), .sel(irmovl_2_out));
  Multiplexer #(.width(4)) multiplexer_3 (
    .in0(_3rd_Reg), .in1(_1st_Reg), .out(MR_RM_Reg_Address), .sel(rmmovl_2_out), .en(or_1_out));
  Multiplexer #(.width(8), .enable("false")) multiplexer_4 (
    .in0({_1st_Reg, _2nd_Reg}), .in1({_2nd_Reg, _3rd_Reg}), .out(multiplexer_4_out), .sel(Instruction[3]));
  Demultiplexer #(.width(8), .enable("false")) demultiplexer_3 (
    .out0(Address_Bus), .out1(Data_Bus), .in(multiplexer_4_out), .sel(Instruction[4]));

  assign Data_1[3:0] = _1st_Reg;
  assign Data_2 = {_2nd_Reg, _3rd_Reg};

  // Other names for the same wires on the sheet: rmmovl = Instruction[3]; immovl = Instruction[4]

  // Notes on the sheet:
  //   Op Code (already dealt with)
  //   If rmmvol or mrmovl
  //   move address to
  //   address bus
  //   Else, put nothing on address bus
  //   and activate given registers appropriately
  //   if mrmovl, activate "3rd Register"
  //   If not rmmovl or mrmovl, use all 3 of these register
  //   If rmmovl, activate "1st Register"
  //   nop
  //   halt
  //   mrmovl
  //   rmmovl
  //   addl
  //   mull
  //   irmovl
  //   If irmovl, move b11..b8 to data bus
  //   instead of address bus
  //   Will send register through to match instruction rm or mr movl
endmodule

// IF
module Instruction_Fetch (
  input  Fetch_First,
  input  Fetch_Second,
  input  StepUp_1,
  input  StepUp2,
  output ROM_LOAD,
  output ALU_A_READ,
  output ALU_B_READ_READ_0,
  output ID_A_READ,
  output ID_B_READ,
  output [7:0] Instruction_Address,
  output Instruction_Read
);

  wire button_1_out, clock_1_out, or_3_out, or_4_out;
  wire [7:0] adder_1_out, adder_2_out, register_1_q;

  or or_1 (ALU_A_READ, Fetch_First, Fetch_Second);
  or or_2 (Instruction_Read, Fetch_Second, StepUp_1);
  or or_3 (or_3_out, StepUp_1, StepUp2);
  Register register_1 (.D(adder_1_out), .en(or_3_out), .Q(register_1_q), .clk(clock_1_out));  // open: clr
  Clock clock_1 (.out(clock_1_out));
  Button button_1 (.out(button_1_out));
  Adder adder_1 (.a(register_1_q), .b(8'h1), .out(adder_1_out));  // open: cin, cout
  Multiplexer #(.width(8)) multiplexer_1 (
    .in0(register_1_q), .in1(adder_2_out), .out(Instruction_Address), .sel(Fetch_Second), .en(or_4_out));
  Adder adder_2 (.a(register_1_q), .b(8'h1), .out(adder_2_out));  // open: cin, cout
  or or_4 (or_4_out, Fetch_First, Fetch_Second);

  assign ALU_B_READ_READ_0 = ALU_A_READ;
  assign ID_A_READ = Fetch_Second;
  assign ID_B_READ = StepUp_1;
  assign ROM_LOAD = ALU_A_READ;
endmodule

module CONTROL (
  input  [15:0] COUNTER_IN,
  input  [6:0] Instruction,
  output RAM_LOAD,
  output RAM_STORE,
  output ALU_A_READ,
  output ALU_B_READ,
  output ALU_B_0,
  output Reg_Write,
  output nMr_rM_1_Reg,
  output nMr_rM_1_Reg_2_3_Reg,
  output n2_3_Reg,
  output nReg_Route,
  output Multiply,
  output Rotue_B,
  output out_15,
  output out_16,
  output out_17,
  output out_18
);

  wire ALU_A_R, and_2_out, and_3_out, and_4_out, and_5_out, and_6_out, and_7_out, and_8_out, and_9_out,
       and_10_out, and_11_out, and_12_out, and_13_out, and_14_out, and_15_out, and_16_out, and_17_out,
       and_18_out, and_19_out, and_20_out, and_21_out, and_22_out, and_23_out, and_24_out, and_25_out,
       and_26_out, and_27_out, and_28_out, and_29_out, and_30_out, and_31_out, and_32_out, or_1_out;

  PC pc_1 ();  // open: Count_Enable, Counter_Value, out_4, out_5, out_6, out_7, out_8, COUNTER_OUT, out_10, out_11, out_12, out_13, out_14, out_15, out_16, out_17, out_18, out_19, out_20, Reset
  Multiplexer multiplexer_1 (.in1(or_1_out), .out(ALU_A_R), .sel(or_1_out), .en(or_1_out));  // open: in0
  or or_1 (or_1_out, COUNTER_IN[1], COUNTER_IN[2]);
  // AND_Gate and_1 has open pins: in0=Instruction[5], in1=COUNTER_IN[4], out=open
  and and_2 (and_2_out, Instruction[5], COUNTER_IN[6]);
  and and_3 (and_3_out, Instruction[6], COUNTER_IN[4]);
  and and_4 (and_4_out, Instruction[6], COUNTER_IN[5]);
  and and_5 (and_5_out, Instruction[5], COUNTER_IN[6]);
  and and_6 (and_6_out, Instruction[6], COUNTER_IN[6]);
  and and_7 (and_7_out, Instruction[5], COUNTER_IN[5]);
  and and_8 (and_8_out, Instruction[6], COUNTER_IN[5]);
  and and_9 (and_9_out, Instruction[5], COUNTER_IN[4]);
  and and_10 (and_10_out, Instruction[5], COUNTER_IN[4]);
  and and_11 (and_11_out, Instruction[5], COUNTER_IN[5]);
  and and_12 (and_12_out, Instruction[6], COUNTER_IN[6]);
  and and_13 (and_13_out, Instruction[6], COUNTER_IN[4]);
  and and_14 (and_14_out, Instruction[5], COUNTER_IN[4]);
  and and_15 (and_15_out, Instruction[6], COUNTER_IN[5]);
  and and_16 (and_16_out, Instruction[5], COUNTER_IN[5]);
  and and_17 (and_17_out, Instruction[5], COUNTER_IN[6]);
  and and_18 (and_18_out, Instruction[6], COUNTER_IN[4]);
  and and_19 (and_19_out, Instruction[6], COUNTER_IN[6]);
  and and_20 (and_20_out, Instruction[2], COUNTER_IN[4]);
  and and_21 (and_21_out, Instruction[2], COUNTER_IN[4]);
  and and_22 (and_22_out, Instruction[2], COUNTER_IN[4]);
  and and_23 (and_23_out, Instruction[2], COUNTER_IN[4]);
  and and_24 (and_24_out, Instruction[2], COUNTER_IN[5]);
  and and_25 (and_25_out, Instruction[2], COUNTER_IN[5]);
  and and_26 (and_26_out, Instruction[2], COUNTER_IN[5]);
  and and_27 (and_27_out, Instruction[6], COUNTER_IN[6]);
  and and_28 (and_28_out, Instruction[5], COUNTER_IN[6]);
  and and_29 (and_29_out, Instruction[2], COUNTER_IN[5]);
  and and_30 (and_30_out, Instruction[6], COUNTER_IN[6]);
  and and_31 (and_31_out, Instruction[6], COUNTER_IN[6]);
  and and_32 (and_32_out, Instruction[5], COUNTER_IN[6]);
  or or_2 (ALU_A_READ, and_21_out, COUNTER_IN[1], COUNTER_IN[2], and_3_out, and_10_out);
  or or_3 (ALU_B_READ, and_22_out, COUNTER_IN[1], COUNTER_IN[2], and_4_out, and_11_out);
  or or_4 (ALU_B_0, and_23_out, COUNTER_IN[1], COUNTER_IN[2]);
  or or_5 (Reg_Write, and_24_out, and_12_out, and_5_out);
  or or_6 (nMr_rM_1_Reg, and_25_out, and_13_out, and_14_out);
  or or_7 (nMr_rM_1_Reg_2_3_Reg, and_26_out, and_15_out, and_6_out, and_16_out, and_17_out);
  or or_8 (n2_3_Reg, and_27_out, and_28_out);
  or or_9 (nReg_Route, and_7_out, and_29_out, and_18_out, and_2_out, and_8_out, and_19_out, and_9_out);
  buf or_10 (Multiply, and_30_out);  // OR_Gate
  or or_11 (Rotue_B, and_31_out, and_32_out);
  buf or_12 (RAM_LOAD, and_20_out);  // OR_Gate
  buf or_13 (RAM_STORE, 1'b0);  // OR_Gate

  assign out_15 = COUNTER_IN[5];
  assign out_16 = COUNTER_IN[6];
  assign out_17 = COUNTER_IN[7];
  assign out_18 = COUNTER_IN[8];

  // Other names for the same wires on the sheet: ALU_B_NAUGHT = ALU_A_R; ALU_B_R = ALU_A_R; _1 = COUNTER_IN[1];
  //   _2 = COUNTER_IN[2]; _4 = COUNTER_IN[4]; _5 = COUNTER_IN[5]; _6 = COUNTER_IN[6]; _7 = COUNTER_IN[7];
  //   _8 = COUNTER_IN[8]; nop = Instruction[0]; halt = Instruction[1]; nmrmovl = Instruction[2];
  //   rmmovl = Instruction[3]; irmovl = Instruction[4]; addl = Instruction[5]; mull = Instruction[6]
endmodule

module Data_Router (
  input  Data_Select,
  input  [7:0] External_Data_In,
  input  [7:0] External_Data_In_2,
  input  Instruction_Read,
  input  [7:0] Register_In,
  input  Mr_rM_1_Reg,
  input  [7:0] ALU_In,
  input  [7:0] Control_In,
  input  [3:0] MR_RM_Reg_Address,
  input  [3:0] _1st_Reg,
  input  [3:0] _2nd_Reg,
  input  [3:0] _3rd_Reg,
  input  Mr_rM_1_Reg_2_3_Reg,
  input  _2_3_Reg,
  output [7:0] Instruction,
  output [7:0] External_Data_Out,
  output [7:0] ALU_Data,
  output [7:0] Register_Out,
  output [3:0] Reg_Select
);

  wire [3:0] multiplexer_2_out, multiplexer_3_out;

  Demultiplexer #(.width(8), .enable("false")) demultiplexer_1 (
    .out0(Register_Out), .out1(Instruction), .in(ALU_In), .sel(Instruction_Read));
  Multiplexer #(.width(8), .enable("false")) multiplexer_1 (
    .in0(External_Data_In), .in1(Register_In), .out(ALU_Data), .sel(Data_Select));
  Multiplexer #(.width(4), .enable("false")) multiplexer_2 (
    .in0(MR_RM_Reg_Address), .in1(_1st_Reg), .out(multiplexer_2_out), .sel(Mr_rM_1_Reg));
  Multiplexer #(.width(4), .enable("false")) multiplexer_3 (
    .in0(_2nd_Reg), .in1(_3rd_Reg), .out(multiplexer_3_out), .sel(_2_3_Reg));
  Multiplexer #(.width(4), .enable("false")) multiplexer_4 (
    .in0(multiplexer_2_out), .in1(multiplexer_3_out), .out(Reg_Select), .sel(Mr_rM_1_Reg_2_3_Reg));
endmodule

module PC (
  input  Count_Enable,
  input  Reset,
  output [7:0] Counter_Value,
  output out_4,
  output out_5,
  output out_6,
  output out_7,
  output out_8,
  output [15:0] COUNTER_OUT,
  output out_10,
  output out_11,
  output out_12,
  output out_13,
  output out_14,
  output out_15,
  output out_16,
  output out_17,
  output out_18,
  output out_19,
  output out_20
);

  wire clock_1_out, Reset_t;

  Clock clock_1 (.out(clock_1_out));
  Counter counter_1 (
    .load(Count_Enable), .D({8{1'b0}}), .count(1'b1), .Q(Counter_Value), .clk(clock_1_out), .clr(Reset));  // open: carry
  and _0 (COUNTER_OUT[0], ~Counter_Value[0], ~Counter_Value[1], ~Counter_Value[2], ~Counter_Value[3]);  // AND_Gate
  and _8 (COUNTER_OUT[8], ~Counter_Value[0], ~Counter_Value[1], ~Counter_Value[2], Counter_Value[3]);  // AND_Gate
  and _16 (Reset_t, Counter_Value[0], ~Counter_Value[1], ~Counter_Value[2], ~Counter_Value[3], ~Counter_Value[5]);  // AND_Gate
  and _1 (COUNTER_OUT[1], Counter_Value[0], ~Counter_Value[1], ~Counter_Value[2], ~Counter_Value[3]);  // AND_Gate
  and _9 (COUNTER_OUT[9], Counter_Value[0], ~Counter_Value[1], ~Counter_Value[2], Counter_Value[3]);  // AND_Gate
  and _2 (COUNTER_OUT[2], ~Counter_Value[0], Counter_Value[1], ~Counter_Value[2], ~Counter_Value[3]);  // AND_Gate
  and _10 (COUNTER_OUT[10], ~Counter_Value[0], Counter_Value[1], ~Counter_Value[2], Counter_Value[3]);  // AND_Gate
  and _3 (COUNTER_OUT[3], Counter_Value[0], Counter_Value[1], ~Counter_Value[2], ~Counter_Value[3]);  // AND_Gate
  and _11 (COUNTER_OUT[11], Counter_Value[0], Counter_Value[1], ~Counter_Value[2], Counter_Value[3]);  // AND_Gate
  and _4 (COUNTER_OUT[4], ~Counter_Value[0], ~Counter_Value[1], Counter_Value[2], ~Counter_Value[3]);  // AND_Gate
  and _12 (COUNTER_OUT[12], ~Counter_Value[0], ~Counter_Value[1], Counter_Value[2], Counter_Value[3]);  // AND_Gate
  and _5 (COUNTER_OUT[5], Counter_Value[0], ~Counter_Value[1], Counter_Value[2], ~Counter_Value[3]);  // AND_Gate
  and _13 (COUNTER_OUT[13], Counter_Value[0], ~Counter_Value[1], Counter_Value[2], Counter_Value[3]);  // AND_Gate
  and _6 (COUNTER_OUT[6], ~Counter_Value[0], Counter_Value[1], Counter_Value[2], ~Counter_Value[3]);  // AND_Gate
  and _14 (COUNTER_OUT[14], ~Counter_Value[0], Counter_Value[1], Counter_Value[2], Counter_Value[3]);  // AND_Gate
  and _7 (COUNTER_OUT[7], Counter_Value[0], Counter_Value[1], Counter_Value[2], ~Counter_Value[3]);  // AND_Gate
  and _15 (COUNTER_OUT[15], Counter_Value[0], Counter_Value[1], Counter_Value[2], Counter_Value[3]);

  assign out_4 = COUNTER_OUT[0];
  assign out_5 = COUNTER_OUT[1];
  assign out_6 = COUNTER_OUT[2];
  assign out_7 = COUNTER_OUT[3];
  assign out_8 = COUNTER_OUT[4];
  assign out_10 = COUNTER_OUT[5];
  assign out_11 = COUNTER_OUT[6];
  assign out_12 = COUNTER_OUT[7];
  assign out_13 = COUNTER_OUT[8];
  assign out_14 = COUNTER_OUT[9];
  assign out_15 = COUNTER_OUT[10];
  assign out_16 = COUNTER_OUT[11];
  assign out_17 = COUNTER_OUT[12];
  assign out_18 = COUNTER_OUT[13];
  assign out_19 = COUNTER_OUT[14];
  assign out_20 = COUNTER_OUT[15];

  // Other names for the same wires on the sheet: _0 = Counter_Value[0]; _1 = Counter_Value[1]; _2 = Counter_Value[2];
  //   _3 = Counter_Value[3]; _4 = Counter_Value[4]; _5 = Counter_Value[5]; _6 = Counter_Value[6];
  //   _7 = Counter_Value[7]
endmodule

// Incr
module _8BitUpCounter (
  input  Enable,
  output [7:0] OUT
);

  wire button_1_out, clock_1_out;
  wire [7:0] adder_1_out;

  Register register_1 (.D(adder_1_out), .en(Enable), .Q(OUT), .clk(clock_1_out), .clr(button_1_out));
  Clock clock_1 (.out(clock_1_out));
  Button button_1 (.out(button_1_out));
  Adder adder_1 (.a(OUT), .b(8'h1), .out(adder_1_out));  // open: cin, cout
endmodule
