// Logisim project bidirect_bus_example.circ as structural Verilog: 1 circuit, main circuit main
module main (
  input  direction_switch,
  input  \input ,
  output \output 
);

  wire not_1_out;

  not not_1 (not_1_out, direction_switch);
  assign \output  = direction_switch ? \input  : 1'bz;  // Controlled_Buffer controlled_buffer_1
  assign \input  = not_1_out ? \output  : 1'bz;  // Controlled_Buffer controlled_buffer_2

  // Notes on the sheet:
  //   (just exchange pins to run in other direction)
endmodule
