// Logisim project prob1.circ as structural Verilog: 2 circuits, main circuit prob1.2
module prob1_2 (
  input  in_1,
  input  [4:0] in_2,
  input  [4:0] in_3,
  input  cnt,
  input  [4:0] in_5,
  input  [4:0] in_6
);

  wire and_1_out, and_2_out, and_3_out, and_4_out, and_5_out, and_6_out, and_7_out, and_8_out, and_9_out,
       and_10_out, and_11_out, and_12_out, and_13_out, and_14_out, and_15_out, and_16_out, and_17_out,
       and_18_out, and_19_out, and_20_out, and_21_out, clock_1_out, multiplexer_1_out, nor_1_out;
  wire [4:0] adder_1_out, multiplexer_2_out, multiplexer_3_out, multiplexer_4_out, register_1_q,
       subtractor_1_out;

  and and_1 (and_1_out, register_1_q[4], ~register_1_q[3], register_1_q[2], ~register_1_q[1], ~register_1_q[0]);  // AND_Gate
  nor nor_1 (nor_1_out, register_1_q[4], register_1_q[3], register_1_q[2], register_1_q[1], register_1_q[0]);
  Multiplexer multiplexer_1 (.in0(and_1_out), .in1(nor_1_out), .out(multiplexer_1_out), .sel(in_1));  // open: en
  Multiplexer #(.width(5)) multiplexer_2 (
    .in0(adder_1_out), .in1(in_2), .out(multiplexer_2_out), .sel(multiplexer_1_out));  // open: en
  Clock clock_1 (.out(clock_1_out));
  Multiplexer #(.width(5)) multiplexer_3 (
    .in0(subtractor_1_out), .in1(in_3), .out(multiplexer_3_out), .sel(multiplexer_1_out));  // open: en
  Multiplexer #(.width(5)) multiplexer_4 (
    .in0(multiplexer_2_out), .in1(multiplexer_3_out), .out(multiplexer_4_out), .sel(in_1));  // open: en
  Register #(.width(5)) register_1 (.D(multiplexer_4_out), .en(cnt), .Q(register_1_q), .clk(clock_1_out));  // open: clr
  and and_2 (and_2_out, register_1_q[4], ~register_1_q[3], register_1_q[2], ~register_1_q[1], ~register_1_q[0]);  // AND_Gate
  LED _20 (.in(and_2_out));
  and and_3 (and_3_out, register_1_q[4], ~register_1_q[3], ~register_1_q[2], register_1_q[1], register_1_q[0]);  // AND_Gate
  LED _19 (.in(and_3_out));
  Subtractor #(.width(5)) subtractor_1 (.a(register_1_q), .b(in_5), .out(subtractor_1_out));  // open: bin, bout
  Adder #(.width(5)) adder_1 (.a(register_1_q), .b(in_6), .out(adder_1_out));  // open: cin, cout
  and and_4 (and_4_out, register_1_q[4], ~register_1_q[3], ~register_1_q[2], register_1_q[1], ~register_1_q[0]);  // AND_Gate
  and and_5 (and_5_out, register_1_q[4], ~register_1_q[3], ~register_1_q[2], ~register_1_q[1], register_1_q[0]);  // AND_Gate
  LED _17 (.in(and_5_out));
  LED _18 (.in(and_4_out));
  and and_6 (and_6_out, register_1_q[4], ~register_1_q[3], ~register_1_q[2], ~register_1_q[1], ~register_1_q[0]);  // AND_Gate
  and and_7 (and_7_out, ~register_1_q[4], register_1_q[3], register_1_q[2], register_1_q[1], register_1_q[0]);  // AND_Gate
  LED _15 (.in(and_7_out));
  LED _16 (.in(and_6_out));
  and and_8 (and_8_out, ~register_1_q[4], register_1_q[3], register_1_q[2], register_1_q[1], ~register_1_q[0]);  // AND_Gate
  LED _14 (.in(and_8_out));
  and and_9 (and_9_out, ~register_1_q[4], register_1_q[3], register_1_q[2], ~register_1_q[1], register_1_q[0]);  // AND_Gate
  and and_10 (and_10_out, ~register_1_q[4], register_1_q[3], register_1_q[2], ~register_1_q[1], ~register_1_q[0]);  // AND_Gate
  LED _12 (.in(and_10_out));
  LED _13 (.in(and_9_out));
  and and_11 (and_11_out, ~register_1_q[4], register_1_q[3], ~register_1_q[2], register_1_q[1], register_1_q[0]);  // AND_Gate
  LED _11 (.in(and_11_out));
  and and_12 (and_12_out, ~register_1_q[4], register_1_q[3], ~register_1_q[2], ~register_1_q[1], register_1_q[0]);  // AND_Gate
  and and_13 (and_13_out, ~register_1_q[4], register_1_q[3], ~register_1_q[2], register_1_q[1], ~register_1_q[0]);  // AND_Gate
  LED _10 (.in(and_13_out));
  LED _9 (.in(and_12_out));
  and and_14 (and_14_out, ~register_1_q[4], register_1_q[3], ~register_1_q[2], ~register_1_q[1], ~register_1_q[0]);  // AND_Gate
  and and_15 (and_15_out, ~register_1_q[4], ~register_1_q[3], register_1_q[2], register_1_q[1], register_1_q[0]);  // AND_Gate
  LED _8 (.in(and_14_out));
  LED _7 (.in(and_15_out));
  and and_16 (and_16_out, ~register_1_q[4], ~register_1_q[3], register_1_q[2], register_1_q[1], ~register_1_q[0]);  // AND_Gate
  LED _6 (.in(and_16_out));
  and and_17 (and_17_out, ~register_1_q[4], ~register_1_q[3], register_1_q[2], ~register_1_q[1], ~register_1_q[0]);  // AND_Gate
  and and_18 (and_18_out, ~register_1_q[4], ~register_1_q[3], register_1_q[2], ~register_1_q[1], register_1_q[0]);  // AND_Gate
  LED _5 (.in(and_18_out));
  LED _4 (.in(and_17_out));
  and and_19 (and_19_out, ~register_1_q[4], ~register_1_q[3], ~register_1_q[2], register_1_q[1], register_1_q[0]);  // AND_Gate
  LED _3 (.in(and_19_out));
  and and_20 (and_20_out, ~register_1_q[4], ~register_1_q[3], ~register_1_q[2], ~register_1_q[1], register_1_q[0]);  // AND_Gate
  and and_21 (and_21_out, ~register_1_q[4], ~register_1_q[3], ~register_1_q[2], register_1_q[1], ~register_1_q[0]);  // AND_Gate
  LED _1 (.in(and_20_out));
  LED _2 (.in(and_21_out));
endmodule

module prob1_3 (
  input  in_1,
  input  [4:0] in_2,
  input  [4:0] in_3,
  input  cnt,
  input  [4:0] in_5,
  input  [4:0] in_6
);

  wire and_1_out, clock_1_out, multiplexer_1_out, nor_1_out;
  wire [4:0] adder_1_out, multiplexer_2_out, multiplexer_3_out, multiplexer_4_out, register_1_q,
       subtractor_1_out;
  wire [19:0] rom_1_data;

  and and_1 (and_1_out, register_1_q[4], ~register_1_q[3], register_1_q[2], ~register_1_q[1], ~register_1_q[0]);  // AND_Gate
  nor nor_1 (nor_1_out, register_1_q[4], register_1_q[3], register_1_q[2], register_1_q[1], register_1_q[0]);
  Multiplexer multiplexer_1 (.in0(and_1_out), .in1(nor_1_out), .out(multiplexer_1_out), .sel(in_1));  // open: en
  Multiplexer #(.width(5)) multiplexer_2 (
    .in0(adder_1_out), .in1(in_2), .out(multiplexer_2_out), .sel(multiplexer_1_out));  // open: en
  Multiplexer #(.width(5)) multiplexer_3 (
    .in0(multiplexer_2_out), .in1(multiplexer_4_out), .out(multiplexer_3_out), .sel(in_1));  // open: en
  Clock clock_1 (.out(clock_1_out));
  Multiplexer #(.width(5)) multiplexer_4 (
    .in0(subtractor_1_out), .in1(in_3), .out(multiplexer_4_out), .sel(multiplexer_1_out));  // open: en
  Register #(.width(5)) register_1 (.D(multiplexer_3_out), .en(cnt), .Q(register_1_q), .clk(clock_1_out));  // open: clr
  Subtractor #(.width(5)) subtractor_1 (.a(register_1_q), .b(in_5), .out(subtractor_1_out));  // open: bin, bout
  Adder #(.width(5)) adder_1 (.a(register_1_q), .b(in_6), .out(adder_1_out));  // open: cin, cout
  ROM #(.addrWidth(5), .dataWidth(20)) rom_1 (.addr(register_1_q), .data(rom_1_data));  // open: sel
  LED led_1 (.in(rom_1_data[19]));
  LED led_2 (.in(rom_1_data[16]));
  LED led_3 (.in(rom_1_data[18]));
  LED led_4 (.in(rom_1_data[17]));
  LED led_5 (.in(rom_1_data[15]));
  LED led_6 (.in(rom_1_data[11]));
  LED led_7 (.in(rom_1_data[12]));
  LED led_8 (.in(rom_1_data[13]));
  LED led_9 (.in(rom_1_data[14]));
  LED led_10 (.in(rom_1_data[7]));
  LED led_11 (.in(rom_1_data[8]));
  LED led_12 (.in(rom_1_data[10]));
  LED led_13 (.in(rom_1_data[9]));
  LED led_14 (.in(rom_1_data[6]));
  LED led_15 (.in(rom_1_data[4]));
  LED led_16 (.in(rom_1_data[5]));
  LED led_17 (.in(rom_1_data[3]));
  LED led_18 (.in(rom_1_data[2]));
  LED led_19 (.in(rom_1_data[0]));
  LED led_20 (.in(rom_1_data[1]));

  // Notes on the sheet:
  //   contents of rom_1 (hex, n*v repeats v):
  //   0 1 2 4 8 10 20 40 80 100 200 400 800 1000 2000 4000 8000 10000 20000 40000 80000
endmodule
