// Logisim project prob2.circ as structural Verilog
module Bidirectional_Test (
  input  in_1,
  input  in_2,
  input  in_3,
  input  in_4,
  input  in_5,
  input  in_6,
  input  in_7,
  input  in_8,
  input  in_9
);

  wire and_1_out, and_2_out, and_3_out, and_4_out, not_1_out, not_2_out, not_3_out;
  wire [7:0] controlled_buffer_5_out, controlled_buffer_6_out;

  not not_1 (not_1_out, in_1);
  assign in_3 = in_1 ? in_2 : 1'bz;  // Controlled_Buffer controlled_buffer_1
  assign in_2 = not_1_out ? in_3 : 1'bz;  // Controlled_Buffer controlled_buffer_2
  and and_1 (and_1_out, in_6, in_7);
  not not_2 (not_2_out, in_6);
  assign in_9 = and_1_out ? in_8 : 1'bz;  // Controlled_Buffer controlled_buffer_3
  and and_2 (and_2_out, in_7, not_2_out);
  assign in_8 = and_2_out ? in_9 : 1'bz;  // Controlled_Buffer controlled_buffer_4
  and and_3 (and_3_out, in_4, in_5);
  not not_3 (not_3_out, in_4);
  and and_4 (and_4_out, in_5, not_3_out);
  assign controlled_buffer_5_out = and_3_out ? controlled_buffer_6_out : 8'bz;  // Controlled_Buffer controlled_buffer_5
  assign controlled_buffer_6_out = and_4_out ? controlled_buffer_5_out : 8'bz;  // Controlled_Buffer controlled_buffer_6
endmodule

module Main (
  input  [7:0] in_1,
  input  in_2,
  input  in_3,
  input  ADC_Latch_Write_Enable,
  input  [7:0] ADC,
  input  in_6,
  input  [7:0] in_7,
  output MAXV,
  output [7:0] out_9,
  output WRITING_TO_BUS,
  output WRITING,
  output [7:0] out_12,
  output [7:0] out_13
);

  wire clock_1_out, clock_2_out, not_1_out, READ_out, s;
  wire [7:0] controlled_buffer_2_out, controlled_buffer_3_out, controlled_buffer_4_out,
       controlled_buffer_5_out, controlled_buffer_6_out, counter_1_q, decoder_1_output, n8bitlatch_1_output,
       n8buffer_1_aout, n8buffer_1_bout, rom_1_data, undriven;

  _8Ltc u_8ltc_1 (.Input(in_7), .READ(1'b1), .SET(s), .WRITE(in_6), .WRITING_TO_BUS(WRITING), .Output(out_13));
  Counter counter_1 (
    .load(MAXV), .D(in_1), .count(1'b1), .Q(counter_1_q), .carry(MAXV), .clk(clock_1_out));  // open: clr
  Clock clock_1 (.out(clock_1_out));
  Button SET (.out(s));
  ROM_part rom_1 (.addr(counter_1_q), .data(rom_1_data));  // open: sel
  assign out_13 = 1'b1 ? rom_1_data : 8'bz;  // Controlled_Buffer controlled_buffer_1
  assign controlled_buffer_2_out = in_2 ? out_12 : 8'bz;  // Controlled_Buffer controlled_buffer_2
  RAM_part ram_1 (.addr(undriven), .data(controlled_buffer_2_out), .clk(clock_1_out), .ld(in_2));  // open: sel, clr
  assign controlled_buffer_3_out = in_3 ? n8buffer_1_bout : 8'bz;  // Controlled_Buffer controlled_buffer_3
  assign controlled_buffer_4_out = not_1_out ? controlled_buffer_3_out : 8'bz;  // Controlled_Buffer controlled_buffer_4
  _8Buffer u_8buffer_1 (
    .BOut(n8buffer_1_bout), .AIn(controlled_buffer_4_out), .READ(READ_out), .DirectionSelect(not_1_out),
    .SET(s), .BIn(controlled_buffer_5_out), .AOut(n8buffer_1_aout));
  assign controlled_buffer_5_out = in_3 ? controlled_buffer_6_out : 8'bz;  // Controlled_Buffer controlled_buffer_5
  assign controlled_buffer_6_out = not_1_out ? n8buffer_1_aout : 8'bz;  // Controlled_Buffer controlled_buffer_6
  not not_1 (not_1_out, in_3);
  Button READ (.out(READ_out));
  Decoder decoder_1 (.OUTPUT(decoder_1_output), ._8_Bit_Address_Bus__Unidirectional(out_13), .WRITE(out_13[7]));
  _8BitLatch u_8bitlatch_1 (
    .Input(ADC), .Output(n8bitlatch_1_output), .READ(out_13[6]), .SET(s), .WRITING_TO_BUS(WRITING_TO_BUS));
  assign out_12 = ADC_Latch_Write_Enable ? n8bitlatch_1_output : 8'bz;  // Controlled_Buffer controlled_buffer_7
  Clock clock_2 (.out(clock_2_out));
  D_Flip_Flop d_ff_1 (.clk(clock_2_out), .D(decoder_1_output[0]), .Q(out_9[0]));  // open: Qn, preset, en, reset
  D_Flip_Flop d_ff_2 (.clk(clock_2_out), .D(decoder_1_output[1]), .Q(out_9[1]));  // open: Qn, preset, en, reset
  D_Flip_Flop d_ff_3 (.clk(clock_2_out), .D(decoder_1_output[2]), .Q(out_9[2]));  // open: Qn, preset, en, reset
  D_Flip_Flop d_ff_4 (.clk(clock_2_out), .D(decoder_1_output[3]), .Q(out_9[3]));  // open: Qn, preset, en, reset
  D_Flip_Flop d_ff_5 (.clk(clock_2_out), .D(decoder_1_output[4]), .Q(out_9[4]));  // open: Qn, preset, en, reset
  D_Flip_Flop d_ff_6 (.clk(clock_2_out), .D(decoder_1_output[5]), .Q(out_9[5]));  // open: Qn, preset, en, reset
  D_Flip_Flop d_ff_7 (.clk(clock_2_out), .D(decoder_1_output[6]), .Q(out_9[6]));  // open: Qn, preset, en, reset

  // Notes on the sheet:
  //   Increments our ROM to deliver sequential instructions
  //   ADDRESS
  //   CONTROL
  //   In a sense, acts as our microprocessor for control.
  //   It delivers Instructions to the control and adress buses
  //   80 is write, 40 is read
  //   Load TESTRUN for the ROM
  //   ROM Write Enable
  //   DATA
  //   contents of rom_1 (hex, n*v repeats v):
  //   0 80 8 88 4 84 c 8c 2 82 a 8a 6 86
  //   Failed Buffer Design
endmodule

// Memory
module MemoryAndBuses (
  input  [7:0] in_1,
  input  [7:0] in_2,
  input  in_3,
  input  in_4,
  input  in_5,
  output [7:0] out_6
);

  wire clock_1_out, not_1_out;

  assign out_6 = in_5 ? in_1 : 8'bz;  // Controlled_Buffer controlled_buffer_1
  Clock clock_1 (.out(clock_1_out));
  not not_1 (not_1_out, in_5);
  RAM_part ram_1 (.addr(in_2), .data(out_6), .sel(in_3), .clk(clock_1_out), .ld(not_1_out), .clr(in_4));

  // Notes on the sheet:
  //   0 is Read, 1 is Load, X is High-State
endmodule

module RAM (
  input  [7:0] in_1,
  input  [7:0] in_2,
  input  in_3,
  input  in_4,
  input  in_5,
  output [7:0] out_6
);

  wire clock_1_out, not_1_out;

  assign out_6 = in_5 ? in_1 : 8'bz;  // Controlled_Buffer controlled_buffer_1
  Clock clock_1 (.out(clock_1_out));
  not not_1 (not_1_out, in_5);
  RAM_part ram_1 (.addr(in_2), .data(out_6), .sel(in_3), .clk(clock_1_out), .ld(not_1_out), .clr(in_4));
endmodule

module ROM (
  input  [7:0] in_1,
  input  in_2,
  output [7:0] out_3
);

  ROM_part rom_1 (.addr(in_1), .data(out_3), .sel(in_2));
endmodule

module Decoder (
  input  WRITE,
  input  [7:0] _8_Bit_Address_Bus__Unidirectional,
  output [7:0] OUTPUT
);

  wire and_1_out, and_2_out, and_3_out, and_4_out, and_5_out, and_6_out, and_7_out, not_1_out, not_2_out,
       not_3_out, not_4_out, not_5_out, not_6_out, not_7_out, not_8_out, not_9_out, not_10_out, not_11_out,
       not_12_out, not_13_out, not_14_out, not_15_out, not_16_out, not_17_out, not_18_out, not_19_out;

  not not_1 (not_1_out, _8_Bit_Address_Bus__Unidirectional[0]);
  not not_2 (not_2_out, _8_Bit_Address_Bus__Unidirectional[1]);
  not not_3 (not_3_out, _8_Bit_Address_Bus__Unidirectional[2]);
  not not_4 (not_4_out, _8_Bit_Address_Bus__Unidirectional[3]);
  not not_5 (not_5_out, _8_Bit_Address_Bus__Unidirectional[0]);
  not not_6 (not_6_out, _8_Bit_Address_Bus__Unidirectional[1]);
  not not_7 (not_7_out, _8_Bit_Address_Bus__Unidirectional[2]);
  not not_8 (not_8_out, _8_Bit_Address_Bus__Unidirectional[0]);
  not not_9 (not_9_out, _8_Bit_Address_Bus__Unidirectional[1]);
  not not_10 (not_10_out, _8_Bit_Address_Bus__Unidirectional[3]);
  not not_11 (not_11_out, _8_Bit_Address_Bus__Unidirectional[0]);
  not not_12 (not_12_out, _8_Bit_Address_Bus__Unidirectional[1]);
  not not_13 (not_13_out, _8_Bit_Address_Bus__Unidirectional[0]);
  not not_14 (not_14_out, _8_Bit_Address_Bus__Unidirectional[2]);
  not not_15 (not_15_out, _8_Bit_Address_Bus__Unidirectional[3]);
  not not_16 (not_16_out, _8_Bit_Address_Bus__Unidirectional[0]);
  not not_17 (not_17_out, _8_Bit_Address_Bus__Unidirectional[2]);
  not not_18 (not_18_out, _8_Bit_Address_Bus__Unidirectional[0]);
  not not_19 (not_19_out, _8_Bit_Address_Bus__Unidirectional[3]);
  and and_1 (and_1_out, not_1_out, not_2_out, not_3_out, not_4_out);
  and and_2 (and_2_out, not_5_out, not_6_out, not_7_out, _8_Bit_Address_Bus__Unidirectional[3]);
  and and_3 (and_3_out, not_8_out, not_9_out, _8_Bit_Address_Bus__Unidirectional[2], not_10_out);
  and and_4 (and_4_out, not_11_out, not_12_out, _8_Bit_Address_Bus__Unidirectional[2], _8_Bit_Address_Bus__Unidirectional[3]);
  and and_5 (and_5_out, not_13_out, _8_Bit_Address_Bus__Unidirectional[1], not_14_out, not_15_out);
  and and_6 (and_6_out, not_16_out, _8_Bit_Address_Bus__Unidirectional[1], not_17_out, _8_Bit_Address_Bus__Unidirectional[3]);
  and and_7 (and_7_out, not_18_out, _8_Bit_Address_Bus__Unidirectional[1], _8_Bit_Address_Bus__Unidirectional[2], not_19_out);
  and and_8 (OUTPUT[0], and_1_out, WRITE);
  and and_9 (OUTPUT[1], and_2_out, WRITE);
  and and_10 (OUTPUT[2], and_3_out, WRITE);
  and and_11 (OUTPUT[3], and_4_out, WRITE);
  and and_12 (OUTPUT[4], and_5_out, WRITE);
  and and_13 (OUTPUT[5], and_6_out, WRITE);
  and and_14 (OUTPUT[6], and_7_out, WRITE);
  and and_15 (OUTPUT[7], _8_Bit_Address_Bus__Unidirectional[7], WRITE);

  // Notes on the sheet:
  //   AC
  //   D0
  //   D1
  //   D2
  //   D3
  //   ES
  //   W
endmodule

// 1Ltch
module _1BitLatch (
  input  SET,
  input  WRITE,
  input  INPUT,
  output OUTPUT
);

  wire and_1_out, and_2_out, nor_1_out, not_1_out, or_1_out;

  not not_1 (not_1_out, INPUT);
  and and_1 (and_1_out, INPUT, INPUT);
  and and_2 (and_2_out, INPUT, not_1_out);
  nor nor_1 (nor_1_out, and_1_out, OUTPUT);
  or or_1 (or_1_out, nor_1_out, SET);
  nor nor_2 (OUTPUT, or_1_out, and_2_out);
endmodule

// 8Ltc
module _8BitLatch (
  input  SET,
  input  READ,
  input  [7:0] Input,
  output WRITING_TO_BUS,
  output [7:0] Output
);

  wire and_1_out, and_2_out, and_3_out, and_4_out, and_5_out, and_6_out, and_7_out, and_8_out, and_9_out,
       and_10_out, and_11_out, and_12_out, and_13_out, and_14_out, and_15_out, and_16_out, nor_1_out,
       nor_3_out, nor_5_out, nor_7_out, nor_9_out, nor_11_out, nor_13_out, nor_15_out, not_1_out, not_2_out,
       not_3_out, not_4_out, not_5_out, not_6_out, not_7_out, not_8_out, or_1_out, or_2_out, or_3_out,
       or_4_out, or_5_out, or_6_out, or_7_out, or_8_out;
  wire [7:0] nor_2_out;

  not not_1 (not_1_out, Input[0]);
  not not_2 (not_2_out, Input[1]);
  not not_3 (not_3_out, Input[2]);
  not not_4 (not_4_out, Input[3]);
  not not_5 (not_5_out, Input[4]);
  not not_6 (not_6_out, Input[5]);
  not not_7 (not_7_out, Input[6]);
  and and_1 (and_1_out, Input[0], READ);
  and and_2 (and_2_out, READ, not_1_out);
  and and_3 (and_3_out, Input[1], READ);
  and and_4 (and_4_out, READ, not_2_out);
  and and_5 (and_5_out, Input[2], READ);
  and and_6 (and_6_out, READ, not_3_out);
  and and_7 (and_7_out, Input[3], READ);
  and and_8 (and_8_out, READ, not_4_out);
  and and_9 (and_9_out, Input[4], READ);
  and and_10 (and_10_out, READ, not_5_out);
  and and_11 (and_11_out, Input[5], READ);
  and and_12 (and_12_out, READ, not_6_out);
  and and_13 (and_13_out, Input[6], READ);
  and and_14 (and_14_out, READ, not_7_out);
  and and_15 (and_15_out, Input[7], READ);
  not not_8 (not_8_out, Input[7]);
  and and_16 (and_16_out, READ, not_8_out);
  nor nor_1 (nor_1_out, and_1_out, nor_2_out[0]);
  or or_1 (or_1_out, nor_1_out, SET);
  nor nor_2 (nor_2_out[0], or_1_out, and_2_out);
  nor nor_3 (nor_3_out, and_3_out, nor_2_out[1]);
  or or_2 (or_2_out, nor_3_out, SET);
  nor nor_4 (nor_2_out[1], or_2_out, and_4_out);
  nor nor_5 (nor_5_out, and_5_out, nor_2_out[2]);
  or or_3 (or_3_out, nor_5_out, SET);
  nor nor_6 (nor_2_out[2], or_3_out, and_6_out);
  nor nor_7 (nor_7_out, and_7_out, nor_2_out[3]);
  or or_4 (or_4_out, nor_7_out, SET);
  nor nor_8 (nor_2_out[3], or_4_out, and_8_out);
  nor nor_9 (nor_9_out, and_9_out, nor_2_out[4]);
  or or_5 (or_5_out, nor_9_out, SET);
  nor nor_10 (nor_2_out[4], or_5_out, and_10_out);
  nor nor_11 (nor_11_out, and_11_out, nor_2_out[5]);
  or or_6 (or_6_out, nor_11_out, SET);
  nor nor_12 (nor_2_out[5], or_6_out, and_12_out);
  nor nor_13 (nor_13_out, and_13_out, nor_2_out[6]);
  or or_7 (or_7_out, nor_13_out, SET);
  nor nor_14 (nor_2_out[6], or_7_out, and_14_out);
  nor nor_15 (nor_15_out, and_15_out, nor_2_out[7]);
  or or_8 (or_8_out, nor_15_out, SET);
  nor nor_16 (nor_2_out[7], or_8_out, and_16_out);
  assign Output = READ ? nor_2_out : 8'bz;  // Controlled_Buffer controlled_buffer_1

  assign WRITING_TO_BUS = READ;
endmodule

// AddLtc
module _8Ltc (
  input  SET,
  input  READ,
  input  WRITE,
  input  [7:0] Input,
  output WRITING_TO_BUS,
  output [7:0] Output
);

  wire and_1_out, and_2_out, and_3_out, and_4_out, and_5_out, and_6_out, and_7_out, and_8_out, and_9_out,
       and_10_out, and_11_out, and_12_out, and_13_out, and_14_out, and_15_out, and_16_out, nor_1_out,
       nor_3_out, nor_5_out, nor_7_out, nor_9_out, nor_11_out, nor_13_out, nor_15_out, not_1_out, not_2_out,
       not_3_out, not_4_out, not_5_out, not_6_out, not_7_out, not_8_out, or_1_out, or_2_out, or_3_out,
       or_4_out, or_5_out, or_6_out, or_7_out, or_8_out;
  wire [7:0] nor_2_out;

  not not_1 (not_1_out, Input[0]);
  not not_2 (not_2_out, Input[1]);
  not not_3 (not_3_out, Input[2]);
  not not_4 (not_4_out, Input[3]);
  not not_5 (not_5_out, Input[4]);
  not not_6 (not_6_out, Input[5]);
  not not_7 (not_7_out, Input[6]);
  and and_1 (and_1_out, Input[0], READ);
  and and_2 (and_2_out, READ, not_1_out);
  and and_3 (and_3_out, Input[1], READ);
  and and_4 (and_4_out, READ, not_2_out);
  and and_5 (and_5_out, Input[2], READ);
  and and_6 (and_6_out, READ, not_3_out);
  and and_7 (and_7_out, Input[3], READ);
  and and_8 (and_8_out, READ, not_4_out);
  and and_9 (and_9_out, Input[4], READ);
  and and_10 (and_10_out, READ, not_5_out);
  and and_11 (and_11_out, Input[5], READ);
  and and_12 (and_12_out, READ, not_6_out);
  and and_13 (and_13_out, Input[6], READ);
  and and_14 (and_14_out, READ, not_7_out);
  and and_15 (and_15_out, Input[7], READ);
  not not_8 (not_8_out, Input[7]);
  and and_16 (and_16_out, READ, not_8_out);
  nor nor_1 (nor_1_out, and_1_out, nor_2_out[0]);
  or or_1 (or_1_out, nor_1_out, SET);
  nor nor_2 (nor_2_out[0], or_1_out, and_2_out);
  nor nor_3 (nor_3_out, and_3_out, nor_2_out[1]);
  or or_2 (or_2_out, nor_3_out, SET);
  nor nor_4 (nor_2_out[1], or_2_out, and_4_out);
  nor nor_5 (nor_5_out, and_5_out, nor_2_out[2]);
  or or_3 (or_3_out, nor_5_out, SET);
  nor nor_6 (nor_2_out[2], or_3_out, and_6_out);
  nor nor_7 (nor_7_out, and_7_out, nor_2_out[3]);
  or or_4 (or_4_out, nor_7_out, SET);
  nor nor_8 (nor_2_out[3], or_4_out, and_8_out);
  nor nor_9 (nor_9_out, and_9_out, nor_2_out[4]);
  or or_5 (or_5_out, nor_9_out, SET);
  nor nor_10 (nor_2_out[4], or_5_out, and_10_out);
  nor nor_11 (nor_11_out, and_11_out, nor_2_out[5]);
  or or_6 (or_6_out, nor_11_out, SET);
  nor nor_12 (nor_2_out[5], or_6_out, and_12_out);
  nor nor_13 (nor_13_out, and_13_out, nor_2_out[6]);
  or or_7 (or_7_out, nor_13_out, SET);
  nor nor_14 (nor_2_out[6], or_7_out, and_14_out);
  nor nor_15 (nor_15_out, and_15_out, nor_2_out[7]);
  or or_8 (or_8_out, nor_15_out, SET);
  nor nor_16 (nor_2_out[7], or_8_out, and_16_out);
  assign Output = WRITE ? nor_2_out : 8'bz;  // Controlled_Buffer controlled_buffer_1

  assign WRITING_TO_BUS = WRITE;
endmodule

module _8Buffer (
  input  READ,
  input  DirectionSelect,
  input  SET,
  input  [7:0] AIn,
  input  [7:0] BIn,
  output [7:0] BOut,
  output [7:0] AOut
);

  wire and_1_out, and_2_out, and_3_out, and_4_out, and_5_out, and_6_out, and_7_out, and_8_out, and_9_out,
       and_10_out, and_11_out, and_12_out, and_13_out, and_14_out, and_15_out, and_16_out, and_17_out,
       and_18_out, and_19_out, and_20_out, and_21_out, and_22_out, and_23_out, and_24_out, and_25_out,
       and_26_out, and_27_out, and_28_out, and_29_out, and_30_out, and_31_out, and_32_out, and_33_out,
       and_34_out, nor_1_out, nor_3_out, nor_5_out, nor_7_out, nor_9_out, nor_11_out, nor_13_out, nor_15_out,
       nor_17_out, nor_19_out, nor_21_out, nor_23_out, nor_25_out, nor_27_out, nor_29_out, nor_31_out,
       not_1_out, not_2_out, not_3_out, not_4_out, not_5_out, not_6_out, not_7_out, not_8_out, not_9_out,
       not_10_out, not_11_out, not_12_out, not_13_out, not_14_out, not_15_out, not_16_out, not_17_out,
       or_1_out, or_2_out, or_3_out, or_4_out, or_5_out, or_6_out, or_7_out, or_8_out, or_9_out, or_10_out,
       or_11_out, or_12_out, or_13_out, or_14_out, or_15_out, or_16_out;

  and and_1 (and_1_out, READ, DirectionSelect);
  not not_1 (not_1_out, AIn[0]);
  not not_2 (not_2_out, AIn[1]);
  not not_3 (not_3_out, AIn[2]);
  not not_4 (not_4_out, AIn[3]);
  not not_5 (not_5_out, AIn[4]);
  not not_6 (not_6_out, AIn[5]);
  not not_7 (not_7_out, AIn[6]);
  and and_2 (and_2_out, AIn[0], and_1_out);
  and and_3 (and_3_out, and_1_out, not_1_out);
  and and_4 (and_4_out, AIn[1], and_1_out);
  and and_5 (and_5_out, and_1_out, not_2_out);
  and and_6 (and_6_out, AIn[2], and_1_out);
  and and_7 (and_7_out, and_1_out, not_3_out);
  and and_8 (and_8_out, AIn[3], and_1_out);
  and and_9 (and_9_out, and_1_out, not_4_out);
  and and_10 (and_10_out, AIn[4], and_1_out);
  and and_11 (and_11_out, and_1_out, not_5_out);
  and and_12 (and_12_out, AIn[5], and_1_out);
  and and_13 (and_13_out, and_1_out, not_6_out);
  and and_14 (and_14_out, AIn[6], and_1_out);
  and and_15 (and_15_out, and_1_out, not_7_out);
  and and_16 (and_16_out, AIn[7], and_1_out);
  not not_8 (not_8_out, AIn[7]);
  and and_17 (and_17_out, and_1_out, not_8_out);
  nor nor_1 (nor_1_out, and_2_out, AOut[0]);
  or or_1 (or_1_out, nor_1_out, SET);
  nor nor_2 (AOut[0], or_1_out, and_3_out);
  nor nor_3 (nor_3_out, and_4_out, AOut[1]);
  or or_2 (or_2_out, nor_3_out, SET);
  nor nor_4 (AOut[1], or_2_out, and_5_out);
  nor nor_5 (nor_5_out, and_6_out, AOut[2]);
  or or_3 (or_3_out, nor_5_out, SET);
  nor nor_6 (AOut[2], or_3_out, and_7_out);
  nor nor_7 (nor_7_out, and_8_out, AOut[3]);
  or or_4 (or_4_out, nor_7_out, SET);
  nor nor_8 (AOut[3], or_4_out, and_9_out);
  nor nor_9 (nor_9_out, and_10_out, AOut[4]);
  or or_5 (or_5_out, nor_9_out, SET);
  nor nor_10 (AOut[4], or_5_out, and_11_out);
  nor nor_11 (nor_11_out, and_12_out, AOut[5]);
  or or_6 (or_6_out, nor_11_out, SET);
  nor nor_12 (AOut[5], or_6_out, and_13_out);
  nor nor_13 (nor_13_out, and_14_out, AOut[6]);
  or or_7 (or_7_out, nor_13_out, SET);
  nor nor_14 (AOut[6], or_7_out, and_15_out);
  nor nor_15 (nor_15_out, and_16_out, AOut[7]);
  or or_8 (or_8_out, nor_15_out, SET);
  nor nor_16 (AOut[7], or_8_out, and_17_out);
  or or_9 (or_9_out, nor_17_out, SET);
  or or_10 (or_10_out, nor_19_out, SET);
  or or_11 (or_11_out, nor_21_out, SET);
  or or_12 (or_12_out, nor_23_out, SET);
  or or_13 (or_13_out, nor_25_out, SET);
  or or_14 (or_14_out, nor_27_out, SET);
  or or_15 (or_15_out, nor_29_out, SET);
  or or_16 (or_16_out, nor_31_out, SET);
  nor nor_17 (nor_17_out, and_18_out, BOut[0]);
  nor nor_18 (BOut[0], or_9_out, and_19_out);
  nor nor_19 (nor_19_out, and_20_out, BOut[1]);
  nor nor_20 (BOut[1], or_10_out, and_21_out);
  nor nor_21 (nor_21_out, and_22_out, BOut[2]);
  nor nor_22 (BOut[2], or_11_out, and_23_out);
  nor nor_23 (nor_23_out, and_24_out, BOut[3]);
  nor nor_24 (BOut[3], or_12_out, and_25_out);
  nor nor_25 (nor_25_out, and_26_out, BOut[4]);
  nor nor_26 (BOut[4], or_13_out, and_27_out);
  nor nor_27 (nor_27_out, and_28_out, BOut[5]);
  nor nor_28 (BOut[5], or_14_out, and_29_out);
  nor nor_29 (nor_29_out, and_30_out, BOut[6]);
  nor nor_30 (BOut[6], or_15_out, and_31_out);
  nor nor_31 (nor_31_out, and_32_out, BOut[7]);
  nor nor_32 (BOut[7], or_16_out, and_33_out);
  and and_18 (and_18_out, BIn[0], and_34_out);
  and and_19 (and_19_out, and_34_out, not_10_out);
  and and_20 (and_20_out, BIn[1], and_34_out);
  and and_21 (and_21_out, and_34_out, not_11_out);
  and and_22 (and_22_out, BIn[2], and_34_out);
  and and_23 (and_23_out, and_34_out, not_12_out);
  and and_24 (and_24_out, BIn[3], and_34_out);
  and and_25 (and_25_out, and_34_out, not_13_out);
  and and_26 (and_26_out, BIn[4], and_34_out);
  and and_27 (and_27_out, and_34_out, not_14_out);
  and and_28 (and_28_out, BIn[5], and_34_out);
  and and_29 (and_29_out, and_34_out, not_15_out);
  and and_30 (and_30_out, BIn[6], and_34_out);
  and and_31 (and_31_out, and_34_out, not_16_out);
  and and_32 (and_32_out, BIn[7], and_34_out);
  and and_33 (and_33_out, and_34_out, not_17_out);
  not not_9 (not_9_out, DirectionSelect);
  and and_34 (and_34_out, READ, not_9_out);
  not not_10 (not_10_out, BIn[0]);
  not not_11 (not_11_out, BIn[1]);
  not not_12 (not_12_out, BIn[2]);
  not not_13 (not_13_out, BIn[3]);
  not not_14 (not_14_out, BIn[4]);
  not not_15 (not_15_out, BIn[5]);
  not not_16 (not_16_out, BIn[6]);
  not not_17 (not_17_out, BIn[7]);
endmodule

module ALU (
  input  [7:0] A_BUS,
  input  [7:0] B_BUS,
  input  F2,
  input  F1,
  input  F0
);
endmodule

// +
module Adder (
  input  [7:0] B,
  input  [7:0] A,
  input  CI,
  output CO,
  output [7:0] OUTPUT
);

  wire and_1_out, and_2_out, and_3_out, and_4_out, and_5_out, and_6_out, and_7_out, and_8_out, and_9_out,
       and_10_out, and_11_out, and_12_out, and_13_out, and_14_out, and_15_out, and_16_out, and_17_out,
       and_18_out, and_19_out, and_20_out, and_21_out, and_22_out, and_23_out, and_24_out, or_2_out,
       or_3_out, or_4_out, or_5_out, or_6_out, or_7_out, or_8_out;

  and and_1 (and_1_out, A[7], B[7]);
  and and_2 (and_2_out, B[7], or_2_out);
  and and_3 (and_3_out, A[7], or_2_out);
  ExactlyOne xor_1 (.out(OUTPUT[7]), .in0(A[7]), .in1(B[7]), .in2(or_2_out));
  or or_1 (CO, and_1_out, and_3_out, and_2_out);
  and and_4 (and_4_out, A[6], or_3_out);
  and and_5 (and_5_out, A[6], B[6]);
  or or_2 (or_2_out, and_5_out, and_4_out, and_6_out);
  and and_6 (and_6_out, B[6], or_3_out);
  ExactlyOne xor_2 (.out(OUTPUT[6]), .in0(A[6]), .in1(B[6]), .in2(or_3_out));
  and and_7 (and_7_out, A[5], or_4_out);
  and and_8 (and_8_out, B[5], or_4_out);
  and and_9 (and_9_out, A[5], B[5]);
  or or_3 (or_3_out, and_9_out, and_7_out, and_8_out);
  and and_10 (and_10_out, A[4], B[4]);
  ExactlyOne xor_3 (.out(OUTPUT[5]), .in0(A[5]), .in1(B[5]), .in2(or_4_out));
  and and_11 (and_11_out, B[4], or_5_out);
  and and_12 (and_12_out, A[4], or_5_out);
  ExactlyOne xor_4 (.out(OUTPUT[4]), .in0(A[4]), .in1(B[4]), .in2(or_5_out));
  or or_4 (or_4_out, and_10_out, and_12_out, and_11_out);
  and and_13 (and_13_out, A[3], B[3]);
  and and_14 (and_14_out, A[3], or_6_out);
  or or_5 (or_5_out, and_13_out, and_14_out, and_15_out);
  and and_15 (and_15_out, B[3], or_6_out);
  and and_16 (and_16_out, A[2], B[2]);
  ExactlyOne xor_5 (.out(OUTPUT[3]), .in0(A[3]), .in1(B[3]), .in2(or_6_out));
  and and_17 (and_17_out, A[2], or_7_out);
  and and_18 (and_18_out, B[2], or_7_out);
  or or_6 (or_6_out, and_16_out, and_17_out, and_18_out);
  and and_19 (and_19_out, A[1], B[1]);
  and and_20 (and_20_out, A[1], or_8_out);
  ExactlyOne xor_6 (.out(OUTPUT[2]), .in0(A[2]), .in1(B[2]), .in2(or_7_out));
  or or_7 (or_7_out, and_19_out, and_20_out, and_21_out);
  and and_21 (and_21_out, B[1], or_8_out);
  ExactlyOne xor_7 (.out(OUTPUT[1]), .in0(A[1]), .in1(B[1]), .in2(or_8_out));
  and and_22 (and_22_out, A[0], B[0]);
  and and_23 (and_23_out, A[0], CI);
  and and_24 (and_24_out, B[0], CI);
  or or_8 (or_8_out, and_22_out, and_23_out, and_24_out);
  ExactlyOne xor_8 (.out(OUTPUT[0]), .in0(A[0]), .in1(B[0]), .in2(CI));
endmodule

module _1BitALExtender (
  input  A,
  input  B,
  input  X,
  input  Y,
  input  Z
);

  // AND_Gate and is placed but not wired
  // OR_Gate or is placed but not wired
endmodule
