// Logisim project prob3.circ as structural Verilog
module Subtractor (
  input  [7:0] in_1,
  input  [7:0] in_2,
  output [7:0] out_3,
  output out_4,
  output [7:0] out_5
);

  Adder adder_1 (.A(in_1), .B(out_3), .CI(1'b1), .CO(out_4), .OUTPUT(out_5));
  assign out_3 = ~in_2;  // NOT_Gate not_1, 8 bits wide
endmodule

// ADD
module Adder (
  input  [7:0] B,
  input  [7:0] A,
  input  CI,
  output CO,
  output [7:0] OUTPUT
);

  wire and_1_out, and_2_out, and_3_out, and_4_out, and_5_out, and_6_out, and_7_out, and_8_out, and_9_out,
       and_10_out, and_11_out, and_12_out, and_13_out, and_14_out, and_15_out, and_16_out, and_17_out,
       and_18_out, and_19_out, and_20_out, and_21_out, and_22_out, and_23_out, and_24_out, or_2_out,
       or_3_out, or_4_out, or_5_out, or_6_out, or_7_out, or_8_out;

  and and_1 (and_1_out, A[7], B[7]);
  and and_2 (and_2_out, A[7], or_2_out);
  and and_3 (and_3_out, B[7], or_2_out);
  ExactlyOne xor_1 (.out(OUTPUT[7]), .in0(A[7]), .in1(B[7]), .in2(or_2_out));
  or or_1 (CO, and_1_out, and_2_out, and_3_out);
  and and_4 (and_4_out, A[6], B[6]);
  and and_5 (and_5_out, A[6], or_3_out);
  or or_2 (or_2_out, and_4_out, and_5_out, and_6_out);
  and and_6 (and_6_out, B[6], or_3_out);
  ExactlyOne xor_2 (.out(OUTPUT[6]), .in0(A[6]), .in1(B[6]), .in2(or_3_out));
  and and_7 (and_7_out, A[5], or_4_out);
  and and_8 (and_8_out, A[5], B[5]);
  and and_9 (and_9_out, B[5], or_4_out);
  or or_3 (or_3_out, and_8_out, and_7_out, and_9_out);
  and and_10 (and_10_out, A[4], B[4]);
  ExactlyOne xor_3 (.out(OUTPUT[5]), .in0(A[5]), .in1(B[5]), .in2(or_4_out));
  and and_11 (and_11_out, B[4], or_5_out);
  and and_12 (and_12_out, A[4], or_5_out);
  ExactlyOne xor_4 (.out(OUTPUT[4]), .in0(A[4]), .in1(B[4]), .in2(or_5_out));
  or or_4 (or_4_out, and_10_out, and_12_out, and_11_out);
  and and_13 (and_13_out, A[3], B[3]);
  and and_14 (and_14_out, A[3], or_6_out);
  or or_5 (or_5_out, and_13_out, and_14_out, and_16_out);
  and and_15 (and_15_out, A[2], B[2]);
  and and_16 (and_16_out, B[3], or_6_out);
  ExactlyOne xor_5 (.out(OUTPUT[3]), .in0(A[3]), .in1(B[3]), .in2(or_6_out));
  and and_17 (and_17_out, A[2], or_7_out);
  and and_18 (and_18_out, B[2], or_7_out);
  or or_6 (or_6_out, and_15_out, and_17_out, and_18_out);
  and and_19 (and_19_out, A[1], B[1]);
  and and_20 (and_20_out, A[1], or_8_out);
  ExactlyOne xor_6 (.out(OUTPUT[2]), .in0(A[2]), .in1(B[2]), .in2(or_7_out));
  or or_7 (or_7_out, and_19_out, and_20_out, and_21_out);
  and and_21 (and_21_out, B[1], or_8_out);
  ExactlyOne xor_7 (.out(OUTPUT[1]), .in0(A[1]), .in1(B[1]), .in2(or_8_out));
  and and_22 (and_22_out, A[0], CI);
  and and_23 (and_23_out, A[0], B[0]);
  and and_24 (and_24_out, B[0], CI);
  or or_8 (or_8_out, and_23_out, and_22_out, and_24_out);
  ExactlyOne xor_8 (.out(OUTPUT[0]), .in0(A[0]), .in1(B[0]), .in2(CI));
endmodule

module Adder_Subtractor (
  input  [7:0] A,
  input  [7:0] B,
  input  SELECT,
  output CARRY,
  output [7:0] OUT
);

  wire [7:0] multiplexer_1_out, not_1_out;

  Adder adder_1 (.A(A), .B(multiplexer_1_out), .CI(SELECT), .CO(CARRY), .OUTPUT(OUT));
  assign not_1_out = ~B;  // NOT_Gate not_1, 8 bits wide
  Multiplexer #(.width(8), .enable("false")) multiplexer_1 (
    .in0(B), .in1(not_1_out), .out(multiplexer_1_out), .sel(SELECT));
endmodule

module BarrelShifter (
  input  [1:0] in_1,
  input  [1:0] in_2,
  input  [1:0] in_3,
  input  [7:0] IN,
  output [7:0] out_5,
  output [7:0] out_6,
  output [7:0] OUT
);

  _4_Bit_Shifter u_4_bit_shifter_1 (.SHIFT(in_3), .IN(IN), .OUT(out_5));
  _2_Bit_Shifter u_2_bit_shifter_1 (.SHIFT(in_2), .IN(out_5), .OUT(out_6));
  _1_Bit_Shifter u_1_bit_shifter_1 (.SHIFT(in_1), .IN(out_6), .OUT(OUT));

  // Notes on the sheet:
  //   0 is Transparent, 1 is Left Shift, 2 is Right Shift
endmodule

// <<>>4
module _4_Bit_Shifter (
  input  [7:0] IN,
  input  [1:0] SHIFT,
  output [7:0] OUT
);

  Multiplexer #(.select(2), .enable("false")) multiplexer_1 (
    .in0(IN[7]), .in1(IN[3]), .in2(1'b0), .out(OUT[7]), .sel(SHIFT));  // open: in3
  Multiplexer #(.select(2), .enable("false")) multiplexer_2 (
    .in0(IN[6]), .in1(IN[2]), .in2(1'b0), .out(OUT[6]), .sel(SHIFT));  // open: in3
  Multiplexer #(.select(2), .enable("false")) multiplexer_3 (
    .in0(IN[5]), .in1(IN[1]), .in2(1'b0), .out(OUT[5]), .sel(SHIFT));  // open: in3
  Multiplexer #(.select(2), .enable("false")) multiplexer_4 (
    .in0(IN[4]), .in1(IN[0]), .in2(1'b0), .out(OUT[4]), .sel(SHIFT));  // open: in3
  Multiplexer #(.select(2), .enable("false")) multiplexer_5 (
    .in0(IN[3]), .in1(1'b0), .in2(IN[7]), .out(OUT[3]), .sel(SHIFT));  // open: in3
  Multiplexer #(.select(2), .enable("false")) multiplexer_6 (
    .in0(IN[2]), .in1(1'b0), .in2(IN[6]), .out(OUT[2]), .sel(SHIFT));  // open: in3
  Multiplexer #(.select(2), .enable("false")) multiplexer_7 (
    .in0(IN[1]), .in1(1'b0), .in2(IN[5]), .out(OUT[1]), .sel(SHIFT));  // open: in3
  Multiplexer #(.select(2), .enable("false")) multiplexer_8 (
    .in0(IN[0]), .in1(1'b0), .in2(IN[4]), .out(OUT[0]), .sel(SHIFT));  // open: in3
endmodule

// <<>>2
module _2_Bit_Shifter (
  input  [7:0] IN,
  input  [1:0] SHIFT,
  output [7:0] OUT
);

  Multiplexer #(.select(2), .enable("false")) multiplexer_1 (
    .in0(IN[7]), .in1(IN[5]), .in2(1'b0), .out(OUT[7]), .sel(SHIFT));  // open: in3
  Multiplexer #(.select(2), .enable("false")) multiplexer_2 (
    .in0(IN[6]), .in1(IN[4]), .in2(1'b0), .out(OUT[6]), .sel(SHIFT));  // open: in3
  Multiplexer #(.select(2), .enable("false")) multiplexer_3 (
    .in0(IN[5]), .in1(IN[3]), .in2(IN[7]), .out(OUT[5]), .sel(SHIFT));  // open: in3
  Multiplexer #(.select(2), .enable("false")) multiplexer_4 (
    .in0(IN[4]), .in1(IN[2]), .in2(IN[6]), .out(OUT[4]), .sel(SHIFT));  // open: in3
  Multiplexer #(.select(2), .enable("false")) multiplexer_5 (
    .in0(IN[3]), .in1(IN[1]), .in2(IN[5]), .out(OUT[3]), .sel(SHIFT));  // open: in3
  Multiplexer #(.select(2), .enable("false")) multiplexer_6 (
    .in0(IN[2]), .in1(IN[0]), .in2(IN[4]), .out(OUT[2]), .sel(SHIFT));  // open: in3
  Multiplexer #(.select(2), .enable("false")) multiplexer_7 (
    .in0(IN[1]), .in1(1'b0), .in2(IN[3]), .out(OUT[1]), .sel(SHIFT));  // open: in3
  Multiplexer #(.select(2), .enable("false")) multiplexer_8 (
    .in0(IN[0]), .in1(1'b0), .in2(IN[2]), .out(OUT[0]), .sel(SHIFT));  // open: in3
endmodule

// <<>>1
module _1_Bit_Shifter (
  input  [7:0] IN,
  input  [1:0] SHIFT,
  output [7:0] OUT
);

  Multiplexer #(.select(2), .enable("false")) multiplexer_1 (
    .in0(IN[7]), .in1(IN[6]), .in2(1'b0), .out(OUT[7]), .sel(SHIFT));  // open: in3
  Multiplexer #(.select(2), .enable("false")) multiplexer_2 (
    .in0(IN[6]), .in1(IN[5]), .in2(IN[7]), .out(OUT[6]), .sel(SHIFT));  // open: in3
  Multiplexer #(.select(2), .enable("false")) multiplexer_3 (
    .in0(IN[5]), .in1(IN[4]), .in2(IN[6]), .out(OUT[5]), .sel(SHIFT));  // open: in3
  Multiplexer #(.select(2), .enable("false")) multiplexer_4 (
    .in0(IN[4]), .in1(IN[3]), .in2(IN[5]), .out(OUT[4]), .sel(SHIFT));  // open: in3
  Multiplexer #(.select(2), .enable("false")) multiplexer_5 (
    .in0(IN[3]), .in1(IN[2]), .in2(IN[4]), .out(OUT[3]), .sel(SHIFT));  // open: in3
  Multiplexer #(.select(2), .enable("false")) multiplexer_6 (
    .in0(IN[2]), .in1(IN[1]), .in2(IN[3]), .out(OUT[2]), .sel(SHIFT));  // open: in3
  Multiplexer #(.select(2), .enable("false")) multiplexer_7 (
    .in0(IN[1]), .in1(IN[0]), .in2(IN[2]), .out(OUT[1]), .sel(SHIFT));  // open: in3
  Multiplexer #(.select(2), .enable("false")) multiplexer_8 (
    .in0(IN[0]), .in1(1'b0), .in2(IN[1]), .out(OUT[0]), .sel(SHIFT));  // open: in3
endmodule
