// Logisim project prob4.circ as structural Verilog: 1 circuit, main circuit main
module main (
  input  a,
  input  in_2,
  input  b,
  input  c,
  input  d,
  output AC,
  output D0,
  output D1,
  output D2,
  output D3,
  output ES,
  output W
);

  wire and_8_out, and_9_out, and_10_out, and_11_out, and_12_out, and_13_out, and_14_out, and_15_out,
       and_16_out, and_17_out, and_18_out, and_19_out, and_20_out, and_21_out, and_22_out, and_23_out,
       and_24_out, and_25_out, and_26_out, and_27_out, and_28_out, and_29_out, and_30_out, and_31_out,
       and_32_out, and_33_out, and_34_out, and_35_out, and_36_out, and_37_out, and_38_out, and_39_out,
       and_40_out, and_41_out, and_42_out, button_1_out, nor_1_out, nor_2_out, nor_3_out, nor_4_out,
       nor_5_out, nor_6_out, nor_7_out, nor_8_out, nor_9_out, nor_10_out, nor_11_out, nor_12_out, nor_13_out,
       nor_14_out, nor_15_out, nor_16_out, nor_17_out, nor_18_out, nor_19_out, nor_20_out, nor_21_out,
       nor_22_out, nor_23_out, nor_24_out, nor_25_out, nor_26_out, nor_27_out, nor_28_out, not_1_out,
       not_2_out, not_3_out, not_4_out, not_5_out, not_6_out, not_7_out, not_8_out, not_9_out, not_10_out,
       not_11_out, not_12_out, not_13_out, not_14_out, not_15_out, not_16_out, not_17_out, not_18_out,
       not_19_out, not_20_out, not_21_out, not_22_out, not_23_out, not_24_out, not_25_out, not_26_out,
       not_27_out, not_28_out, not_29_out, not_30_out, not_31_out, not_32_out, not_33_out, not_34_out,
       not_35_out, not_36_out, not_37_out, not_38_out, not_39_out, not_40_out, or_1_out, or_2_out, or_3_out,
       or_4_out, or_5_out, or_6_out, or_7_out;

  not not_1 (not_1_out, a);
  not not_2 (not_2_out, b);
  not not_3 (not_3_out, c);
  not not_4 (not_4_out, d);
  not not_5 (not_5_out, a);
  not not_6 (not_6_out, b);
  not not_7 (not_7_out, c);
  not not_8 (not_8_out, a);
  not not_9 (not_9_out, b);
  not not_10 (not_10_out, d);
  not not_11 (not_11_out, a);
  not not_12 (not_12_out, b);
  not not_13 (not_13_out, a);
  not not_14 (not_14_out, c);
  not not_15 (not_15_out, d);
  not not_16 (not_16_out, a);
  not not_17 (not_17_out, c);
  not not_18 (not_18_out, a);
  not not_19 (not_19_out, d);
  and and_1 (AC, not_1_out, not_2_out, not_3_out, not_4_out);
  and and_2 (D0, not_5_out, not_6_out, not_7_out, d);
  and and_3 (D1, not_8_out, not_9_out, c, not_10_out);
  and and_4 (D2, not_11_out, not_12_out, c, d);
  and and_5 (D3, not_13_out, b, not_14_out, not_15_out);
  and and_6 (ES, not_16_out, b, not_17_out, d);
  and and_7 (W, not_18_out, b, c, not_19_out);
  and and_8 (and_8_out, AC, in_2);
  and and_9 (and_9_out, D0, in_2);
  and and_10 (and_10_out, D1, in_2);
  and and_11 (and_11_out, D2, in_2);
  and and_12 (and_12_out, D3, in_2);
  and and_13 (and_13_out, ES, in_2);
  and and_14 (and_14_out, W, in_2);
  not not_20 (not_20_out, and_8_out);
  not not_21 (not_21_out, nor_15_out);
  not not_22 (not_22_out, and_9_out);
  not not_23 (not_23_out, nor_17_out);
  not not_24 (not_24_out, and_10_out);
  not not_25 (not_25_out, nor_19_out);
  not not_26 (not_26_out, and_11_out);
  not not_27 (not_27_out, nor_21_out);
  not not_28 (not_28_out, and_12_out);
  not not_29 (not_29_out, nor_23_out);
  not not_30 (not_30_out, and_13_out);
  not not_31 (not_31_out, nor_25_out);
  not not_32 (not_32_out, and_14_out);
  not not_33 (not_33_out, nor_27_out);
  and and_15 (and_15_out, nor_15_out, not_20_out);
  nor nor_1 (nor_1_out, and_15_out, nor_2_out);
  and and_16 (and_16_out, not_20_out, not_21_out);
  nor nor_2 (nor_2_out, nor_1_out, and_16_out);
  and and_17 (and_17_out, nor_17_out, not_22_out);
  nor nor_3 (nor_3_out, and_17_out, nor_4_out);
  and and_18 (and_18_out, not_22_out, not_23_out);
  nor nor_4 (nor_4_out, nor_3_out, and_18_out);
  nor nor_5 (nor_5_out, and_19_out, nor_6_out);
  and and_19 (and_19_out, nor_19_out, not_24_out);
  and and_20 (and_20_out, not_24_out, not_25_out);
  nor nor_6 (nor_6_out, nor_5_out, and_20_out);
  nor nor_7 (nor_7_out, and_21_out, nor_8_out);
  and and_21 (and_21_out, nor_21_out, not_26_out);
  and and_22 (and_22_out, not_26_out, not_27_out);
  nor nor_8 (nor_8_out, nor_7_out, and_22_out);
  nor nor_9 (nor_9_out, and_23_out, nor_10_out);
  and and_23 (and_23_out, nor_23_out, not_28_out);
  and and_24 (and_24_out, not_28_out, not_29_out);
  nor nor_10 (nor_10_out, nor_9_out, and_24_out);
  nor nor_11 (nor_11_out, and_25_out, nor_12_out);
  and and_25 (and_25_out, nor_25_out, not_30_out);
  and and_26 (and_26_out, not_30_out, not_31_out);
  nor nor_12 (nor_12_out, nor_11_out, and_26_out);
  and and_27 (and_27_out, nor_27_out, not_32_out);
  nor nor_13 (nor_13_out, and_27_out, nor_14_out);
  and and_28 (and_28_out, not_32_out, not_33_out);
  nor nor_14 (nor_14_out, nor_13_out, and_28_out);
  not not_34 (not_34_out, nor_2_out);
  not not_35 (not_35_out, nor_4_out);
  not not_36 (not_36_out, nor_6_out);
  not not_37 (not_37_out, nor_8_out);
  not not_38 (not_38_out, nor_10_out);
  not not_39 (not_39_out, nor_12_out);
  not not_40 (not_40_out, nor_14_out);
  and and_29 (and_29_out, nor_2_out, and_8_out);
  and and_30 (and_30_out, and_8_out, not_34_out);
  and and_31 (and_31_out, nor_4_out, and_9_out);
  and and_32 (and_32_out, and_9_out, not_35_out);
  and and_33 (and_33_out, nor_6_out, and_10_out);
  and and_34 (and_34_out, and_10_out, not_36_out);
  and and_35 (and_35_out, nor_8_out, and_11_out);
  and and_36 (and_36_out, and_11_out, not_37_out);
  and and_37 (and_37_out, nor_10_out, and_12_out);
  and and_38 (and_38_out, and_12_out, not_38_out);
  and and_39 (and_39_out, nor_12_out, and_13_out);
  and and_40 (and_40_out, and_13_out, not_39_out);
  and and_41 (and_41_out, nor_14_out, and_14_out);
  and and_42 (and_42_out, and_14_out, not_40_out);
  nor nor_15 (nor_15_out, and_29_out, nor_16_out);
  or or_1 (or_1_out, nor_15_out, button_1_out);
  nor nor_16 (nor_16_out, or_1_out, and_30_out);
  nor nor_17 (nor_17_out, and_31_out, nor_18_out);
  or or_2 (or_2_out, nor_17_out, button_1_out);
  nor nor_18 (nor_18_out, or_2_out, and_32_out);
  nor nor_19 (nor_19_out, and_33_out, nor_20_out);
  or or_3 (or_3_out, nor_19_out, button_1_out);
  nor nor_20 (nor_20_out, or_3_out, and_34_out);
  nor nor_21 (nor_21_out, and_35_out, nor_22_out);
  or or_4 (or_4_out, nor_21_out, button_1_out);
  nor nor_22 (nor_22_out, or_4_out, and_36_out);
  nor nor_23 (nor_23_out, and_37_out, nor_24_out);
  or or_5 (or_5_out, nor_23_out, button_1_out);
  nor nor_24 (nor_24_out, or_5_out, and_38_out);
  nor nor_25 (nor_25_out, and_39_out, nor_26_out);
  or or_6 (or_6_out, nor_25_out, button_1_out);
  nor nor_26 (nor_26_out, or_6_out, and_40_out);
  nor nor_27 (nor_27_out, and_41_out, nor_28_out);
  or or_7 (or_7_out, nor_27_out, button_1_out);
  nor nor_28 (nor_28_out, or_7_out, and_42_out);
  Button button_1 (.out(button_1_out));
  LED led_1 (.in(nor_16_out));
  LED led_2 (.in(nor_18_out));
  LED led_3 (.in(nor_20_out));
  LED led_4 (.in(nor_22_out));
  LED led_5 (.in(nor_24_out));
  LED led_6 (.in(nor_26_out));
  LED led_7 (.in(nor_28_out));

  // Notes on the sheet:
  //   AC
  //   D0
  //   D1
  //   D2
  //   D3
  //   ES
  //   W
endmodule
